// Logisim project FirstVersion.circ as structural Verilog
module start_to_16_bit_shr (
  input  [15:0] value,
  input  [3:0] shift_amount
);

  wire decoder_1_out1, decoder_1_out2, decoder_1_out3, decoder_1_out4, decoder_1_out5, decoder_1_out6,
       decoder_1_out7, decoder_1_out8, decoder_2_out0, decoder_2_out1, decoder_2_out2, decoder_2_out3,
       decoder_2_out4, decoder_2_out5, decoder_2_out6, decoder_2_out7, decoder_3_out0, decoder_3_out1,
       decoder_3_out2, decoder_3_out3, decoder_3_out4, decoder_3_out5, decoder_3_out6, decoder_4_out0,
       decoder_4_out1, decoder_4_out2, decoder_4_out3, decoder_4_out4, decoder_4_out5, decoder_5_out0,
       decoder_5_out1, decoder_5_out2, decoder_5_out3, decoder_5_out4, decoder_6_out0, decoder_6_out1,
       decoder_6_out2, decoder_6_out3, decoder_7_out0, decoder_7_out1, decoder_7_out2, decoder_8_out0,
       decoder_8_out1, decoder_9_out0;
  wire [8:0] decoder_1_out0;

  Decoder #(.select(4), .disabled(0)) decoder_1 (
    .out0(decoder_1_out0[0]), .out1(decoder_1_out1), .out2(decoder_1_out2), .out3(decoder_1_out3),
    .out4(decoder_1_out4), .out5(decoder_1_out5), .out6(decoder_1_out6), .out7(decoder_1_out7),
    .out8(decoder_1_out8), .sel(shift_amount), .en(value[0]));  // open: out9, out10, out11, out12, out13, out14, out15
  Decoder #(.select(4), .disabled(0)) decoder_2 (
    .out0(decoder_2_out0), .out1(decoder_2_out1), .out2(decoder_2_out2), .out3(decoder_2_out3),
    .out4(decoder_2_out4), .out5(decoder_2_out5), .out6(decoder_2_out6), .out7(decoder_2_out7),
    .sel(shift_amount), .en(value[1]));  // open: out8, out9, out10, out11, out12, out13, out14, out15
  Decoder #(.select(4), .disabled(0)) decoder_3 (
    .out0(decoder_3_out0), .out1(decoder_3_out1), .out2(decoder_3_out2), .out3(decoder_3_out3),
    .out4(decoder_3_out4), .out5(decoder_3_out5), .out6(decoder_3_out6), .sel(shift_amount), .en(value[2]));  // open: out7, out8, out9, out10, out11, out12, out13, out14, out15
  Decoder #(.select(4), .disabled(0)) decoder_4 (
    .out0(decoder_4_out0), .out1(decoder_4_out1), .out2(decoder_4_out2), .out3(decoder_4_out3),
    .out4(decoder_4_out4), .out5(decoder_4_out5), .sel(shift_amount), .en(value[3]));  // open: out6, out7, out8, out9, out10, out11, out12, out13, out14, out15
  Decoder #(.select(4), .disabled(0)) decoder_5 (
    .out0(decoder_5_out0), .out1(decoder_5_out1), .out2(decoder_5_out2), .out3(decoder_5_out3),
    .out4(decoder_5_out4), .sel(shift_amount), .en(value[4]));  // open: out5, out6, out7, out8, out9, out10, out11, out12, out13, out14, out15
  Decoder #(.select(4), .disabled(0)) decoder_6 (
    .out0(decoder_6_out0), .out1(decoder_6_out1), .out2(decoder_6_out2), .out3(decoder_6_out3),
    .sel(shift_amount), .en(value[5]));  // open: out4, out5, out6, out7, out8, out9, out10, out11, out12, out13, out14, out15
  Decoder #(.select(4), .disabled(0)) decoder_7 (
    .out0(decoder_7_out0), .out1(decoder_7_out1), .out2(decoder_7_out2), .sel(shift_amount), .en(value[6]));  // open: out3, out4, out5, out6, out7, out8, out9, out10, out11, out12, out13, out14, out15
  Decoder #(.select(4), .disabled(0)) decoder_8 (
    .out0(decoder_8_out0), .out1(decoder_8_out1), .sel(shift_amount), .en(value[7]));  // open: out2, out3, out4, out5, out6, out7, out8, out9, out10, out11, out12, out13, out14, out15
  Decoder #(.select(4), .disabled(0)) decoder_9 (
    .out0(decoder_9_out0), .sel(shift_amount), .en(value[8]));  // open: out1, out2, out3, out4, out5, out6, out7, out8, out9, out10, out11, out12, out13, out14, out15
  Decoder #(.select(4), .disabled(0)) decoder_10 (
    .sel(shift_amount), .en(value[9]));  // open: out0, out1, out2, out3, out4, out5, out6, out7, out8, out9, out10, out11, out12, out13, out14, out15
  Decoder #(.select(4), .disabled(0)) decoder_11 (
    .sel(shift_amount), .en(value[10]));  // open: out0, out1, out2, out3, out4, out5, out6, out7, out8, out9, out10, out11, out12, out13, out14, out15
  Decoder #(.select(4), .disabled(0)) decoder_12 (
    .sel(shift_amount), .en(value[11]));  // open: out0, out1, out2, out3, out4, out5, out6, out7, out8, out9, out10, out11, out12, out13, out14, out15
  Decoder #(.select(4), .disabled(0)) decoder_13 (
    .sel(shift_amount), .en(value[12]));  // open: out0, out1, out2, out3, out4, out5, out6, out7, out8, out9, out10, out11, out12, out13, out14, out15
  Decoder #(.select(4), .disabled(0)) decoder_14 (
    .sel(shift_amount), .en(value[13]));  // open: out0, out1, out2, out3, out4, out5, out6, out7, out8, out9, out10, out11, out12, out13, out14, out15
  Decoder #(.select(4), .disabled(0)) decoder_15 (
    .sel(shift_amount), .en(value[14]));  // open: out0, out1, out2, out3, out4, out5, out6, out7, out8, out9, out10, out11, out12, out13, out14, out15
  Decoder #(.select(4), .disabled(0)) decoder_16 (
    .sel(shift_amount), .en(value[15]));  // open: out0, out1, out2, out3, out4, out5, out6, out7, out8, out9, out10, out11, out12, out13, out14, out15
  or or_1 (decoder_1_out0[1], decoder_1_out1, decoder_2_out0);
  or or_2 (decoder_1_out0[2], decoder_1_out2, decoder_2_out1, decoder_3_out0);
  or or_3 (decoder_1_out0[3], decoder_1_out3, decoder_2_out2, decoder_3_out1, decoder_4_out0);
  or or_4 (decoder_1_out0[4], decoder_1_out4, decoder_2_out3, decoder_3_out2, decoder_4_out1, decoder_5_out0);
  or or_5 (decoder_1_out0[5], decoder_1_out5, decoder_2_out4, decoder_3_out3, decoder_4_out2, decoder_5_out1, decoder_6_out0);
  or or_6 (decoder_1_out0[6], decoder_1_out6, decoder_2_out5, decoder_3_out4, decoder_4_out3, decoder_5_out2, decoder_6_out1, decoder_7_out0);
  or or_7 (decoder_1_out0[7], decoder_1_out7, decoder_2_out6, decoder_3_out5, decoder_4_out4, decoder_5_out3, decoder_6_out2, decoder_7_out1, decoder_8_out0);
  or or_8 (decoder_1_out0[8], decoder_1_out8, decoder_2_out7, decoder_3_out6, decoder_4_out5, decoder_9_out0, decoder_5_out4, decoder_6_out3, decoder_7_out2, decoder_8_out1);
endmodule

module half_adder (
  input  in_1,
  input  in_2,
  output out_3,
  output out_4
);

  xor xor_1 (out_3, in_1, in_2);
  and and_1 (out_4, in_1, in_2);
endmodule

module full_adder (
  input  in_1,
  input  in_2,
  input  in_3,
  output out_4,
  output out_5
);

  wire half_adder_1_out_3, half_adder_1_out_4, half_adder_2_out_4;

  half_adder half_adder_1 (.in_1(in_1), .in_2(in_2), .out_3(half_adder_1_out_3), .out_4(half_adder_1_out_4));
  half_adder half_adder_2 (.in_1(half_adder_1_out_3), .in_2(in_3), .out_3(out_4), .out_4(half_adder_2_out_4));
  or or_1 (out_5, half_adder_1_out_4, half_adder_2_out_4);
endmodule

module _16_bit_adder (
  input  carry_in,
  input  [15:0] a,
  input  [15:0] b,
  output [15:0] carry_out,
  output carry_out_2
);

  wire full_adder_1_out_5, full_adder_2_out_5, full_adder_3_out_5, full_adder_4_out_5, full_adder_5_out_5,
       full_adder_6_out_5, full_adder_7_out_5, full_adder_8_out_5, full_adder_9_out_5, full_adder_10_out_5,
       full_adder_11_out_5, full_adder_12_out_5, full_adder_13_out_5, full_adder_14_out_5,
       full_adder_15_out_5;

  full_adder full_adder_1 (.in_1(carry_in), .in_2(a[0]), .in_3(b[0]), .out_4(carry_out[0]), .out_5(full_adder_1_out_5));
  full_adder full_adder_2 (
    .in_1(full_adder_1_out_5), .in_2(a[1]), .in_3(b[1]), .out_4(carry_out[1]), .out_5(full_adder_2_out_5));
  full_adder full_adder_3 (
    .in_1(full_adder_2_out_5), .in_2(a[2]), .in_3(b[2]), .out_4(carry_out[2]), .out_5(full_adder_3_out_5));
  full_adder full_adder_4 (
    .in_1(full_adder_3_out_5), .in_2(a[3]), .in_3(b[3]), .out_4(carry_out[3]), .out_5(full_adder_4_out_5));
  full_adder full_adder_5 (
    .in_1(full_adder_4_out_5), .in_2(a[4]), .in_3(b[4]), .out_4(carry_out[4]), .out_5(full_adder_5_out_5));
  full_adder full_adder_6 (
    .in_1(full_adder_5_out_5), .in_2(a[5]), .in_3(b[5]), .out_4(carry_out[5]), .out_5(full_adder_6_out_5));
  full_adder full_adder_7 (
    .in_1(full_adder_6_out_5), .in_2(a[6]), .in_3(b[6]), .out_4(carry_out[6]), .out_5(full_adder_7_out_5));
  full_adder full_adder_8 (
    .in_1(full_adder_7_out_5), .in_2(a[7]), .in_3(b[7]), .out_4(carry_out[7]), .out_5(full_adder_8_out_5));
  full_adder full_adder_9 (
    .in_1(full_adder_8_out_5), .in_2(a[8]), .in_3(b[8]), .out_4(carry_out[8]), .out_5(full_adder_9_out_5));
  full_adder full_adder_10 (
    .in_1(full_adder_9_out_5), .in_2(a[9]), .in_3(b[9]), .out_4(carry_out[9]), .out_5(full_adder_10_out_5));
  full_adder full_adder_11 (
    .in_1(full_adder_10_out_5), .in_2(a[10]), .in_3(b[10]), .out_4(carry_out[10]), .out_5(full_adder_11_out_5));
  full_adder full_adder_12 (
    .in_1(full_adder_11_out_5), .in_2(a[11]), .in_3(b[11]), .out_4(carry_out[11]), .out_5(full_adder_12_out_5));
  full_adder full_adder_13 (
    .in_1(full_adder_12_out_5), .in_2(a[12]), .in_3(b[12]), .out_4(carry_out[12]), .out_5(full_adder_13_out_5));
  full_adder full_adder_14 (
    .in_1(full_adder_13_out_5), .in_2(a[13]), .in_3(b[13]), .out_4(carry_out[13]), .out_5(full_adder_14_out_5));
  full_adder full_adder_15 (
    .in_1(full_adder_14_out_5), .in_2(a[14]), .in_3(b[14]), .out_4(carry_out[14]), .out_5(full_adder_15_out_5));
  full_adder full_adder_16 (
    .in_1(full_adder_15_out_5), .in_2(a[15]), .in_3(b[15]), .out_4(carry_out[15]), .out_5(carry_out_2));
endmodule

module _16_bit_add_sub (
  input  carry,
  input  use_carry,
  input  subtract,
  input  [15:0] a,
  input  [15:0] b,
  output [15:0] \output ,
  output carry_out
);

  wire and_1_out, and_2_out, not_1_out, not_2_out, or_1_out;
  wire [15:0] controlled_inverter_1_out;

  and and_1 (and_1_out, carry, use_carry);
  not not_1 (not_1_out, use_carry);
  assign controlled_inverter_1_out = subtract ? ~b : 16'bz;  // Controlled_Inverter controlled_inverter_1
  assign controlled_inverter_1_out = not_2_out ? b : 16'bz;  // Controlled_Buffer controlled_buffer_1
  not not_2 (not_2_out, subtract);
  and and_2 (and_2_out, not_1_out, subtract);
  or or_1 (or_1_out, and_1_out, and_2_out);
  _16_bit_adder u_16_bit_adder_1 (
    .carry_in(or_1_out), .a(a), .b(controlled_inverter_1_out), .carry_out(\output ), .carry_out_2(carry_out));
  // Probe on a
  // Probe on b
  // Probe on \output 
endmodule

module alu (
  input  [15:0] instruction,
  input  carry_in,
  input  [15:0] a,
  input  [15:0] b,
  output zero_out,
  output carry_out,
  output minus_out
);

  wire decoder_1_out0, decoder_1_out1, decoder_1_out2, decoder_1_out3, decoder_1_out4, decoder_1_out5,
       decoder_1_out6, decoder_1_out7, decoder_1_out8, decoder_1_out9, decoder_1_out10, or_2_out;
  wire [14:0] controlled_buffer_1_out;
  wire [15:0] and_1_out, n16_bit_add_sub_1_output, nand_1_out, nor_1_out, or_1_out, xnor_1_out, xor_1_out;

  // Probe on a
  // Probe on b
  // Probe on {minus_out, controlled_buffer_1_out}
  _16_bit_add_sub u_16_bit_add_sub_1 (
    .carry(carry_in), .use_carry(instruction[2]), .subtract(instruction[3]), .a(a), .b(b),
    .\output (n16_bit_add_sub_1_output), .carry_out(carry_out));
  assign and_1_out = a & b;  // AND_Gate and_1, 16 bits wide
  assign or_1_out = a | b;  // OR_Gate or_1, 16 bits wide
  assign nand_1_out = ~(a & b);  // NAND_Gate nand_1, 16 bits wide
  assign nor_1_out = ~(a | b);  // NOR_Gate nor_1, 16 bits wide
  assign xor_1_out = a ^ b;  // XOR_Gate xor_1, 16 bits wide
  assign xnor_1_out = ~(a ^ b);  // XNOR_Gate xnor_1, 16 bits wide
  Shifter #(.width(16), .shift("lr")) shifter_1 ();  // open: in, dist, out
  Shifter shifter_2 ();  // open: in, dist, out
  assign {minus_out, controlled_buffer_1_out} = or_2_out ? n16_bit_add_sub_1_output : 16'bz;  // Controlled_Buffer controlled_buffer_1
  or or_2 (or_2_out, decoder_1_out0, decoder_1_out1, decoder_1_out10, decoder_1_out2, decoder_1_out3);
  assign {minus_out, controlled_buffer_1_out} = decoder_1_out4 ? and_1_out : 16'bz;  // Controlled_Buffer controlled_buffer_2
  assign {minus_out, controlled_buffer_1_out} = decoder_1_out5 ? or_1_out : 16'bz;  // Controlled_Buffer controlled_buffer_3
  assign {minus_out, controlled_buffer_1_out} = decoder_1_out6 ? nand_1_out : 16'bz;  // Controlled_Buffer controlled_buffer_4
  assign {minus_out, controlled_buffer_1_out} = decoder_1_out7 ? nor_1_out : 16'bz;  // Controlled_Buffer controlled_buffer_5
  assign {minus_out, controlled_buffer_1_out} = decoder_1_out8 ? xor_1_out : 16'bz;  // Controlled_Buffer controlled_buffer_6
  assign {minus_out, controlled_buffer_1_out} = decoder_1_out9 ? xnor_1_out : 16'bz;  // Controlled_Buffer controlled_buffer_7
  Decoder #(.select(4), .enable("false")) decoder_1 (
    .out0(decoder_1_out0), .out1(decoder_1_out1), .out2(decoder_1_out2), .out3(decoder_1_out3),
    .out4(decoder_1_out4), .out5(decoder_1_out5), .out6(decoder_1_out6), .out7(decoder_1_out7),
    .out8(decoder_1_out8), .out9(decoder_1_out9), .out10(decoder_1_out10), .sel(instruction[5:2]));  // open: out11, out12, out13, out14, out15
  is_zero is_zero_1 (.in_1({minus_out, controlled_buffer_1_out}), .out_2(zero_out));
endmodule

module is_zero (
  input  [15:0] in_1,
  output out_2
);

  wire or_1_out;

  or or_1 (or_1_out, in_1[0], in_1[1], in_1[2], in_1[3], in_1[4], in_1[5], in_1[6], in_1[7], in_1[8], in_1[9], in_1[10], in_1[11], in_1[12], in_1[13], in_1[14], in_1[15]);
  not not_1 (out_2, or_1_out);
endmodule

module barrel_shifter (
  input  [3:0] a,
  input  [1:0] shift_amount,
  output [3:0] a_2
);

  wire decoder_1_out0, decoder_1_out1, decoder_1_out2, decoder_1_out3;

  Decoder #(.select(2), .enable("false")) decoder_1 (
    .out0(decoder_1_out0), .out1(decoder_1_out1), .out2(decoder_1_out2), .out3(decoder_1_out3),
    .sel(shift_amount));
  assign a_2[3] = decoder_1_out3 ? a[0] : 1'bz;  // Controlled_Buffer controlled_buffer_1
  assign a_2[2] = decoder_1_out2 ? a[0] : 1'bz;  // Controlled_Buffer controlled_buffer_2
  assign a_2[1] = decoder_1_out1 ? a[0] : 1'bz;  // Controlled_Buffer controlled_buffer_3
  assign a_2[0] = decoder_1_out0 ? a[0] : 1'bz;  // Controlled_Buffer controlled_buffer_4
  assign a_2[3] = decoder_1_out2 ? a[1] : 1'bz;  // Controlled_Buffer controlled_buffer_5
  assign a_2[2] = decoder_1_out1 ? a[1] : 1'bz;  // Controlled_Buffer controlled_buffer_6
  assign a_2[1] = decoder_1_out0 ? a[1] : 1'bz;  // Controlled_Buffer controlled_buffer_7
  assign a_2[0] = decoder_1_out3 ? a[1] : 1'bz;  // Controlled_Buffer controlled_buffer_8
  assign a_2[3] = decoder_1_out1 ? a[2] : 1'bz;  // Controlled_Buffer controlled_buffer_9
  assign a_2[2] = decoder_1_out0 ? a[2] : 1'bz;  // Controlled_Buffer controlled_buffer_10
  assign a_2[1] = decoder_1_out3 ? a[2] : 1'bz;  // Controlled_Buffer controlled_buffer_11
  assign a_2[0] = decoder_1_out2 ? a[2] : 1'bz;  // Controlled_Buffer controlled_buffer_12
  assign a_2[3] = decoder_1_out0 ? a[3] : 1'bz;  // Controlled_Buffer controlled_buffer_13
  assign a_2[2] = decoder_1_out3 ? a[3] : 1'bz;  // Controlled_Buffer controlled_buffer_14
  assign a_2[1] = decoder_1_out2 ? a[3] : 1'bz;  // Controlled_Buffer controlled_buffer_15
  assign a_2[0] = decoder_1_out1 ? a[3] : 1'bz;  // Controlled_Buffer controlled_buffer_16
endmodule
